// Logisim project single_cycle_cpu.circ as structural Verilog: 9 circuits, main circuit main
module main (
);

  Registers registers_1 ();  // open: rs1_out, clk, write_enable, read_address, rs2_address, rs1_address, data_in, rs2_out, clr
endmodule

module Registers (
  input  [31:0] data_in,
  input  [4:0] rs1_address,
  input  [4:0] rs2_address,
  input  [4:0] read_address,
  input  write_enable,
  input  clk,
  input  clr,
  output [31:0] rs1_out,
  output [31:0] rs2_out
);

  wire decoder_1_out0, decoder_1_out1, decoder_1_out2, decoder_1_out3, decoder_1_out4, decoder_1_out5,
       decoder_1_out6, decoder_1_out7, decoder_1_out8, decoder_1_out9, decoder_1_out10, decoder_1_out11,
       decoder_1_out12, decoder_1_out13, decoder_1_out14, decoder_1_out15, decoder_1_out16, decoder_1_out17,
       decoder_1_out18, decoder_1_out19, decoder_1_out20, decoder_1_out21, decoder_1_out22, decoder_1_out23,
       decoder_1_out24, decoder_1_out25, decoder_1_out26, decoder_1_out27, decoder_1_out28, decoder_1_out29,
       decoder_1_out30, decoder_1_out31;
  wire [31:0] x0_q, x1_q, x2_q, x3_q, x4_q, x5_q, x6_q, x7_q, x8_q, x9_q, x10_q, x11_q, x12_q, x13_q, x14_q,
       x15_q, x16_q, x17_q, x18_q, x19_q, x20_q, x21_q, x22_q, x23_q, x24_q, x25_q, x26_q, x27_q, x28_q,
       x29_q, x30_q, x31_q;

  Decoder #(.select(5)) decoder_1 (
    .out0(decoder_1_out0), .out1(decoder_1_out1), .out2(decoder_1_out2), .out3(decoder_1_out3),
    .out4(decoder_1_out4), .out5(decoder_1_out5), .out6(decoder_1_out6), .out7(decoder_1_out7),
    .out8(decoder_1_out8), .out9(decoder_1_out9), .out10(decoder_1_out10), .out11(decoder_1_out11),
    .out12(decoder_1_out12), .out13(decoder_1_out13), .out14(decoder_1_out14), .out15(decoder_1_out15),
    .out16(decoder_1_out16), .out17(decoder_1_out17), .out18(decoder_1_out18), .out19(decoder_1_out19),
    .out20(decoder_1_out20), .out21(decoder_1_out21), .out22(decoder_1_out22), .out23(decoder_1_out23),
    .out24(decoder_1_out24), .out25(decoder_1_out25), .out26(decoder_1_out26), .out27(decoder_1_out27),
    .out28(decoder_1_out28), .out29(decoder_1_out29), .out30(decoder_1_out30), .out31(decoder_1_out31),
    .sel(read_address), .en(write_enable));
  Register #(.width(32)) x0 (.D({32{1'b0}}), .en(decoder_1_out0), .clk(clk), .Q(x0_q), .clr(clr));
  Register #(.width(32)) x1 (.D(data_in), .en(decoder_1_out1), .clk(clk), .Q(x1_q), .clr(clr));
  Register #(.width(32)) x2 (.D(data_in), .en(decoder_1_out2), .clk(clk), .Q(x2_q), .clr(clr));
  Register #(.width(32)) x3 (.D(data_in), .en(decoder_1_out3), .clk(clk), .Q(x3_q), .clr(clr));
  Register #(.width(32)) x4 (.D(data_in), .en(decoder_1_out4), .clk(clk), .Q(x4_q), .clr(clr));
  Register #(.width(32)) x5 (.D(data_in), .en(decoder_1_out5), .clk(clk), .Q(x5_q), .clr(clr));
  Register #(.width(32)) x6 (.D(data_in), .en(decoder_1_out6), .clk(clk), .Q(x6_q), .clr(clr));
  Register #(.width(32)) x7 (.D(data_in), .en(decoder_1_out7), .clk(clk), .Q(x7_q), .clr(clr));
  Register #(.width(32)) x8 (.D(data_in), .en(decoder_1_out8), .clk(clk), .Q(x8_q), .clr(clr));
  Register #(.width(32)) x9 (.D(data_in), .en(decoder_1_out9), .clk(clk), .Q(x9_q), .clr(clr));
  Register #(.width(32)) x10 (.D(data_in), .en(decoder_1_out10), .clk(clk), .Q(x10_q), .clr(clr));
  Register #(.width(32)) x11 (.D(data_in), .en(decoder_1_out11), .clk(clk), .Q(x11_q), .clr(clr));
  Register #(.width(32)) x12 (.D(data_in), .en(decoder_1_out12), .clk(clk), .Q(x12_q), .clr(clr));
  Register #(.width(32)) x13 (.D(data_in), .en(decoder_1_out13), .clk(clk), .Q(x13_q), .clr(clr));
  Register #(.width(32)) x14 (.D(data_in), .en(decoder_1_out14), .clk(clk), .Q(x14_q), .clr(clr));
  Register #(.width(32)) x15 (.D(data_in), .en(decoder_1_out15), .clk(clk), .Q(x15_q), .clr(clr));
  Register #(.width(32)) x16 (.D(data_in), .en(decoder_1_out16), .clk(clk), .Q(x16_q), .clr(clr));
  Register #(.width(32)) x17 (.D(data_in), .en(decoder_1_out17), .clk(clk), .Q(x17_q), .clr(clr));
  Register #(.width(32)) x18 (.D(data_in), .en(decoder_1_out18), .clk(clk), .Q(x18_q), .clr(clr));
  Register #(.width(32)) x19 (.D(data_in), .en(decoder_1_out19), .clk(clk), .Q(x19_q), .clr(clr));
  Register #(.width(32)) x20 (.D(data_in), .en(decoder_1_out20), .clk(clk), .Q(x20_q), .clr(clr));
  Register #(.width(32)) x21 (.D(data_in), .en(decoder_1_out21), .clk(clk), .Q(x21_q), .clr(clr));
  Register #(.width(32)) x22 (.D(data_in), .en(decoder_1_out22), .clk(clk), .Q(x22_q), .clr(clr));
  Register #(.width(32)) x23 (.D(data_in), .en(decoder_1_out23), .clk(clk), .Q(x23_q), .clr(clr));
  Register #(.width(32)) x24 (.D(data_in), .en(decoder_1_out24), .clk(clk), .Q(x24_q), .clr(clr));
  Register #(.width(32)) x25 (.D(data_in), .en(decoder_1_out25), .clk(clk), .Q(x25_q), .clr(clr));
  Register #(.width(32)) x26 (.D(data_in), .en(decoder_1_out26), .clk(clk), .Q(x26_q), .clr(clr));
  Register #(.width(32)) x27 (.D(data_in), .en(decoder_1_out27), .clk(clk), .Q(x27_q), .clr(clr));
  Register #(.width(32)) x28 (.D(data_in), .en(decoder_1_out28), .clk(clk), .Q(x28_q), .clr(clr));
  Register #(.width(32)) x29 (.D(data_in), .en(decoder_1_out29), .clk(clk), .Q(x29_q), .clr(clr));
  Register #(.width(32)) x30 (.D(data_in), .en(decoder_1_out30), .clk(clk), .Q(x30_q), .clr(clr));
  Register #(.width(32)) x31 (.D(data_in), .en(decoder_1_out31), .clk(clk), .Q(x31_q), .clr(clr));
  Multiplexer #(.select(5), .width(32), .enable("false")) multiplexer_1 (
    .in0(x0_q), .in1(x1_q), .in2(x2_q), .in3(x3_q), .in4(x4_q), .in5(x5_q), .in6(x6_q), .in7(x7_q),
    .in8(x8_q), .in9(x9_q), .in10(x10_q), .in11(x11_q), .in12(x12_q), .in13(x13_q), .in14(x14_q),
    .in15(x15_q), .in16(x16_q), .in17(x17_q), .in18(x18_q), .in19(x19_q), .in20(x20_q), .in21(x21_q),
    .in22(x22_q), .in23(x23_q), .in24(x24_q), .in25(x25_q), .in26(x26_q), .in27(x27_q), .in28(x28_q),
    .in29(x29_q), .in30(x30_q), .in31(x31_q), .out(rs1_out), .sel(rs1_address));
  Multiplexer #(.select(5), .width(32), .enable("false")) multiplexer_2 (
    .in0(x0_q), .in1(x1_q), .in2(x2_q), .in3(x3_q), .in4(x4_q), .in5(x5_q), .in6(x6_q), .in7(x7_q),
    .in8(x8_q), .in9(x9_q), .in10(x10_q), .in11(x11_q), .in12(x12_q), .in13(x13_q), .in14(x14_q),
    .in15(x15_q), .in16(x16_q), .in17(x17_q), .in18(x18_q), .in19(x19_q), .in20(x20_q), .in21(x21_q),
    .in22(x22_q), .in23(x23_q), .in24(x24_q), .in25(x25_q), .in26(x26_q), .in27(x27_q), .in28(x28_q),
    .in29(x29_q), .in30(x30_q), .in31(x31_q), .out(rs2_out), .sel(rs2_address));

  // Other names for the same wires on the sheet: d_in[31:0] = data_in
endmodule

module Logic_Unit (
  input  [3:0] ALU_selection
);

  z32B_Adder z32b_adder_1 ();  // open: c_out, sum, c_in, b, a

  // Other names for the same wires on the sheet: SEL[3:0] = ALU_selection

  // Notes on the sheet:
  //   arithmetic
  //   add
  //   sub
endmodule

module z1B_Adder (
  input  a,
  input  b,
  input  c_in,
  output sum,
  output c_out
);

  wire and_1_out, and_2_out, xor_1_out;

  xor xor_1 (xor_1_out, a, b);
  xor xor_2 (sum, xor_1_out, c_in);
  and and_1 (and_1_out, a, b);
  and and_2 (and_2_out, xor_1_out, c_in);
  or or_1 (c_out, and_1_out, and_2_out);
endmodule

module z2B_Adder (
  input  [1:0] a,
  input  [1:0] b,
  input  c_in,
  output [1:0] sum,
  output c_out
);

  wire z1b_adder_1_c_out;

  z1B_Adder z1b_adder_1 (.a(a[0]), .b(b[0]), .c_in(c_in), .sum(sum[0]), .c_out(z1b_adder_1_c_out));
  z1B_Adder z1b_adder_2 (.a(a[1]), .b(b[1]), .c_in(z1b_adder_1_c_out), .sum(sum[1]), .c_out(c_out));
endmodule

module z4B_Adder (
  input  [3:0] a,
  input  [3:0] b,
  input  c_in,
  output [3:0] sum,
  output c_out
);

  wire z2b_adder_1_c_out;

  z2B_Adder z2b_adder_1 (.a(a[1:0]), .b(b[1:0]), .c_in(c_in), .sum(sum[1:0]), .c_out(z2b_adder_1_c_out));
  z2B_Adder z2b_adder_2 (.a(a[3:2]), .b(b[3:2]), .c_in(z2b_adder_1_c_out), .sum(sum[3:2]), .c_out(c_out));
endmodule

module z8B_Adder (
  input  [7:0] a,
  input  [7:0] b,
  input  c_in,
  output [7:0] sum,
  output c_out
);

  wire z4b_adder_1_c_out;

  z4B_Adder z4b_adder_1 (.a(a[3:0]), .b(b[3:0]), .c_in(c_in), .sum(sum[3:0]), .c_out(z4b_adder_1_c_out));
  z4B_Adder z4b_adder_2 (.a(a[7:4]), .b(b[7:4]), .c_in(z4b_adder_1_c_out), .sum(sum[7:4]), .c_out(c_out));
endmodule

module z16B_Adder (
  input  [15:0] a,
  input  [15:0] b,
  input  c_in,
  output [15:0] sum,
  output c_out
);

  wire z8b_adder_1_c_out;

  z8B_Adder z8b_adder_1 (.a(a[7:0]), .b(b[7:0]), .c_in(c_in), .sum(sum[7:0]), .c_out(z8b_adder_1_c_out));
  z8B_Adder z8b_adder_2 (.a(a[15:8]), .b(b[15:8]), .c_in(z8b_adder_1_c_out), .sum(sum[15:8]), .c_out(c_out));
endmodule

module z32B_Adder (
  input  [31:0] a,
  input  [31:0] b,
  input  c_in,
  output [31:0] sum,
  output c_out
);

  wire z16b_adder_1_c_out;

  z16B_Adder z16b_adder_1 (.a(a[15:0]), .b(b[15:0]), .c_in(c_in), .sum(sum[15:0]), .c_out(z16b_adder_1_c_out));
  z16B_Adder z16b_adder_2 (.a(a[31:16]), .b(b[31:16]), .c_in(z16b_adder_1_c_out), .sum(sum[31:16]), .c_out(c_out));
endmodule
